# Fritzing sketch full system (saved by Fritzing 0.9.3b)
breadboards: 1

parts:
  Keypad4x1 = Keypad Membran 4x4
  Part1 = Arduino Uno (Rev3)
  Part2 = RFID-RC522-v2
  LCM1602_IIC1 = LCM1602 IIC [part_number="LCM1602 IIC" chip_label="LCM1602 IIC" package="DIP (Dual Inline) [THT]"]
  LCD1 = LCD screen
  J1 = Basic Servo
  J2 = Piezo Speaker
  LED1 = LED - 5mm [color="Red (633nm)" package="5 mm [THT]"]
  LED2 = LED - 5mm [color="Blue (430nm)" package="5 mm [THT]"]
  LED3 = LED - 5mm [color="Green (555nm)" package="5 mm [THT]"]
  R1 = Resistor [tolerance=±5% resistance=220 package=THT]
  R2 = Resistor [tolerance=±5% resistance=220 package=THT]
  R3 = Resistor [tolerance=±5% resistance=220 package=THT]
  Part3 = Arduino Uno (Rev3)
  U1 = OV7670 Camera [package=camera_sfv24r-2st_2]
  Part4 = HC-SR501 Body Sensor Module
  R4 = Resistor [tolerance=±5% resistance=4.7k package=THT]
  R5 = Resistor [tolerance=±5% resistance=4.7k package=THT]
  R6 = Resistor [tolerance=±5% resistance=10k package=THT]
  R7 = Resistor [tolerance=±5% resistance=10k package=THT]
  J3 = Power Jack [package=power_jack_pth_lock]  # not connected
  VCC1 = 4 x AAA Battery Mount  # not connected

nets:
  N1: Keypad4x1.Pin1, Part1.A0
  N2: Keypad4x1.Pin2, Part1.A1
  N3: Keypad4x1.Pin3, Part1.A2
  N4: Keypad4x1.Pin4, Part1.A3
  N5: Keypad4x1.Pin5, Part1.D2
  N6: Keypad4x1.Pin6, Part1.D1/TX
  N7: Keypad4x1.Pin7, Part1.D0/RX
  N8: Part1.A4/SDA, LCM1602_IIC1.SDA
  N9: Part1.A5/SCL, LCM1602_IIC1.SCL
  N10: Part1.D8, J1.pulse
  N11: Part1.D9_PWM, Part2.RST
  N12: Part1.D10_PWM/SS, Part2.SDA
  N13: Part1.D11_PWM/MOSI, Part2.MOSI
  N14: Part1.D12/MISO, Part2.MISO
  N15: Part1.D13/SCK, Part2.SCK
  GND: Part1.GND, Part2.GND, LCM1602_IIC1.GND, J1.gnd, J2.pin1, R1.Pin_1, R2.Pin_1, R3.Pin_1
  N16: Part1.D4, Part3.D12/MISO
  N17: Part1.D5_PWM, J2.pin2
  N18: Part1.D6_PWM, LED1.anode
  N19: Part1.D7, LED3.anode
  N20: Part1.ioref, J1.vcc, LED2.anode
  3V3: Part1.3V3, Part2.3.3V
  5V: Part1.5V, LCM1602_IIC1.VCC
  VSS: LCM1602_IIC1.VSS, LCD1.VSS
  VDD: LCM1602_IIC1.VDD, LCD1.VDD
  N21: LCM1602_IIC1.V0, LCD1.V0
  N22: LCM1602_IIC1.RS, LCD1.RS
  N23: LCM1602_IIC1.RW, LCD1.R/W
  N24: LCM1602_IIC1.E, LCD1.E
  N25: LCM1602_IIC1.D0, LCD1.DB0
  N26: LCM1602_IIC1.D1, LCD1.DB1
  N27: LCM1602_IIC1.D2, LCD1.DB2
  N28: LCM1602_IIC1.D3, LCD1.DB3
  N29: LCM1602_IIC1.D4, LCD1.DB4
  N30: LCM1602_IIC1.D5, LCD1.DB5
  N31: LCM1602_IIC1.D6, LCD1.DB6
  N32: LCM1602_IIC1.D7, LCD1.DB7
  N33: LCM1602_IIC1.A, LCD1.LED+
  N34: LCM1602_IIC1.K, LCD1.LED-
  N35: LCM1602_IIC1.LED_A, LCM1602_IIC1.LED_B
  N36: LED1.cathode, R2.Pin_0
  N37: LED2.cathode, R3.Pin_0
  N38: LED3.cathode, R1.Pin_0
  N39: Part3.A0, U1.D0
  N40: Part3.A1, U1.D1
  N41: Part3.A2, U1.D2
  N42: Part3.A3, U1.D3
  N43: Part3.A4/SDA, U1.SIDO, R6.Pin_0
  N44: Part3.A5/SCL, U1.SIOC, R7.Pin_0
  N45: Part3.D8, U1.HREF
  N46: Part3.D11_PWM/MOSI, R5.Pin_0
  N47: Part3.D13/SCK, Part4.OUT
  GND_2: Part3.GND, U1.GND, U1.PWDN, Part4.GND, R4.Pin_1
  N48: Part3.D2, U1.PCLK
  N49: Part3.D3_PWM, U1.VSYNC
  N50: Part3.D4, U1.D4
  N51: Part3.D5_PWM, U1.D5
  N52: Part3.D6_PWM, U1.D6
  N53: Part3.D7, U1.D7
  3V3_2: Part3.3V3, U1.3V3, U1.RESET, Part4.VCC, R6.Pin_1, R7.Pin_1
  N54: U1.XCLK, R4.Pin_0, R5.Pin_1

custom parts:
  Keypad Membran 4x4: Membrane Keypad 4x4 Matrix
  RFID-RC522-v2: A simple China made RFID-RC522 Reader; do check the pin labels, as this is a MFRC522 based clone.
  LCM1602 IIC: I2C-Module to use a 1602 or 2004 LCD on with the wire.h libory Serial LCD Modul
  OV7670 Camera: CMOS image sensor
  HC-SR501 Body Sensor Module: Pyroelectric Infrared PIR Motion Sensor Detector Module
